# Fritzing sketch pirrigation (saved by Fritzing 0.9.3b)
breadboards: 1

parts:
  VCC1 = 4 x AAA Battery Mount
  Q1 = NPN-Transistor [package="SOT-23 [SMD]"]
  M1 = DC Motor
  Raspberry_Pi1 = Raspberry Pi B+
  D1 = Rectifier Diode [part_number=1N4001 package="300 mil [THT]"]
  R1 = Resistor [tolerance=±5% resistance=1k package=THT]
  R2 = Resistor [tolerance=±5% resistance=1k package=THT]

nets:
  N1: VCC1.-, Q1.2, R2.Pin_0
  D9358: VCC1.+, M1.pin_1, D1.anode
  N2: Q1.0, R1.Pin_0
  N3: Q1.1, M1.pin_2, D1.cathode
  N4: Raspberry_Pi1.GPIO26, R1.Pin_1
  N5: Raspberry_Pi1.GND, R2.Pin_1
